# Fritzing sketch Timelapse Camera Release (saved by Fritzing 0.9.3b)

parts:
  Bauteil1 = Arduino Nano (Rev3.0)
  Bauteil2 = Adafruit DS3231 [part_number="Adafruit #3013"]
  SW1 = DIP Switch 8 Position [package=dipswitch-08]
  U1 = Optocoupler [package=THT]
  R2 = Resistor [tolerance=±5% resistance=220 package=THT]
  U5 = 2.5mm Audio Jack [package=stereojack2.5mm_specia_pogopins]

nets:
  GND: Bauteil1.GND, Bauteil2.GND, SW1.11, SW1.12, SW1.13, SW1.14, SW1.15, SW1.16, U1.Pin_2
  N1: Bauteil1.D2, R2.Pin_0
  N2: Bauteil1.D8, SW1.5
  N3: Bauteil1.D9, SW1.4
  N4: Bauteil1.D10, SW1.3
  N5: Bauteil1.D11/MOSI, SW1.2
  N6: Bauteil1.D12/MISO, SW1.1
  5V: Bauteil1.5V, Bauteil2.Vin
  N7: Bauteil1.A5, Bauteil2.SCL
  N8: Bauteil1.A4, Bauteil2.SDA
  N9: U1.Pin_1, R2.Pin_1
  N10: U1.Pin_4, U5.SLEEVE
  N11: U1.Pin_5, U5.LEFT, U5.RIGHT

notes:
  Camera Adapter
  Mini Jack (2.5mm)

custom parts:
  Adafruit DS3231: The datasheet for the DS3231 explains that this part is an "Extremely Accurate I²C-Integrated RTC/TCXO/Crystal". And, hey, it does exactly what it says on the tin! This Real Time Clock (RTC) is the most precise you can get in a small, low power package. Most RTCs use an external 32kHz timing crystal that is used to keep time with low current draw. And that's all well and good, but those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
